# Fritzing sketch LCD (saved by Fritzing 0.9.3b)
breadboards: 1

parts:
  부품1 = Arduino Mega ADK (Rev3)
  LCD1 = LCD screen
  R1 = Rotary Potentiometer (Small) [maximum_resistance=100kΩ package=THT]

nets:
  GND: 부품1.GND, LCD1.VSS, LCD1.R/W, LCD1.LED-, R1.leg1
  N1: 부품1.D13_PWM, LCD1.DB7
  N2: 부품1.D12_PWM, LCD1.DB6
  N3: 부품1.D11_PWM, LCD1.DB5
  N4: 부품1.D10_PWM, LCD1.DB4
  5V: 부품1.5V, LCD1.VDD, LCD1.LED+, R1.leg2
  N5: 부품1.D3_PWM, LCD1.RS
  N6: 부품1.D4_PWM, LCD1.E
  N7: LCD1.V0, R1.wiper
