# Fritzing sketch flower_led_project (saved by Fritzing 0.9.2b)
breadboards: 1

parts:
  부품1 = Arduino Uno (Rev3)
  LED1 = LED - 5mm [color="Red (635nm)" package="5 mm [THT]"]
  R1 = Resistor [tolerance=±5% resistance=220 package=THT]
  R2 = Rotary Potentiometer (Small) [maximum_resistance=100kΩ package=THT]

nets:
  N1: 부품1.A0, R2.wiper
  N2: 부품1.D13/SCK, R1.Pin_0
  N3: 부품1.5V, R2.leg1
  N4: 부품1.GND, LED1.cathode, R2.leg2
  N5: LED1.anode, R1.Pin_1
