# Fritzing sketch wifi_fire (saved by Fritzing 0.9.3b)
breadboards: 1

parts:
  부품1 = Arduino Mega ADK (Rev3)  # not connected
  부품2 = Arduino Ethernet Shield (Rev3)
  LED1 = LED - 5mm [color="Red (633nm)" package="5 mm [THT]"]
  R1 = Resistor [tolerance=±5% resistance=220 package=THT]

nets:
  N1: 부품2.SPI/D12, R1.Pin_0
  N2: 부품2.D2, 부품2.5V
  N3: 부품2.GND, LED1.cathode
  N4: LED1.anode, R1.Pin_1
