# Fritzing sketch wifi_motor (saved by Fritzing 0.9.3b)
breadboards: 1

parts:
  부품3 = Arduino Mega ADK (Rev3)  # not connected
  부품4 = Arduino Ethernet Shield (Rev3)
  LED1 = LED - 5mm [color="Red (633nm)" package="5 mm [THT]"]
  R1 = Resistor [tolerance=±5% resistance=220 package=THT]
  J1 = Basic Servo

nets:
  N1: 부품4.PWM_D9, J1.pulse
  N2: 부품4.SPI/D12, R1.Pin_0
  5V: 부품4.5V, J1.vcc
  GND: 부품4.GND, LED1.cathode, J1.gnd
  N3: LED1.anode, R1.Pin_1
