# Fritzing sketch BluetoothTest (saved by Fritzing 0.9.3b)
breadboards: 1

parts:
  부품1 = Arduino Uno (Rev3)
  R1 = Rotary Potentiometer (Small) [maximum_resistance=100kΩ package=THT]
  R2 = Resistor [tolerance=±5% resistance=220 package=THT]
  LED1 = LED - 5mm [color="Red (633nm)" package="5 mm [THT]"]

nets:
  N1: 부품1.A0, R1.wiper
  N2: 부품1.D7, R2.Pin_1
  N3: 부품1.5V, R1.leg2
  N4: 부품1.GND, R1.leg1, LED1.cathode
  N5: R2.Pin_0, LED1.anode
